// Logisim project Ex1.circ as structural Verilog: 1 circuit, main circuit main
module main (
  input  AND_Gate,
  input  in_2,
  input  in_3,
  input  in_4,
  input  in_5,
  input  OR_Gate,
  input  NAND_Gate,
  input  in_8,
  input  in_9,
  input  in_10,
  input  in_11,
  input  in_12,
  input  in_13,
  output out_14,
  output out_15,
  output out_16,
  output out_17,
  output out_18,
  output out_19,
  output out_20
);

  not not_1 (out_14, in_2);
  or or_1 (out_17, OR_Gate, in_9);
  and and_1 (out_15, AND_Gate, in_4);
  nand nand_1 (out_18, NAND_Gate, in_10);
  nor nor_1 (out_20, in_12, in_13);
  xor xor_1 (out_16, in_3, in_5);
  xnor xnor_1 (out_19, in_8, in_11);

  // Notes on the sheet:
  //   NOT Gate
  //   NOR Gate
  //   XOR Gate
  //   XNOR Gate
endmodule
