// Logisim project Ex2.circ as structural Verilog: 1 circuit, main circuit main
module main (
  input  A,
  input  A_2,
  input  B,
  input  B_2,
  input  in_5,
  input  in_6,
  output Output,
  output Output_2,
  output out_9
);

  wire nand_1_out, nand_2_out, nand_3_out, nor_1_out;

  nand nand_1 (nand_1_out, A, A);
  nand nand_2 (nand_2_out, B_2, B_2);
  nand nand_3 (nand_3_out, in_5, in_6);
  nand nand_4 (Output, nand_1_out, nand_2_out);
  nand nand_5 (out_9, nand_3_out, nand_3_out);
  nor nor_1 (nor_1_out, A_2, B);
  nor nor_2 (Output_2, nor_1_out, nor_1_out);

  // Notes on the sheet:
  //   EXERCISE #2
  //   Circuit #1
  //   Verify that the truth tables for Circuit #1 and Circuit #2 are equivalent
  //   Create an equivalent circuit to circuit#3  using NOR gates (Remember DeMorgan's Theorem)
  //   Yes, both circuit 1 & 2 are equivalent
  //   Circuit #2
endmodule
