// Logisim project Ex3.circ as structural Verilog: 1 circuit, main circuit main
module main (
  input  in_1,
  input  in_2,
  output out_3,
  output out_4
);

  wire nand_1_out, nand_2_out, nand_3_out, nand_4_out, nand_5_out;

  not nand_1 (nand_1_out, in_2);  // NAND_Gate
  not nand_2 (nand_2_out, in_1);  // NAND_Gate
  nand nand_3 (nand_3_out, nand_1_out, in_1);
  nand nand_4 (nand_4_out, nand_2_out, in_2);
  nand nand_5 (nand_5_out, in_2, in_1);
  nand nand_6 (out_3, nand_3_out, nand_4_out);
  not nand_7 (out_4, nand_5_out);  // NAND_Gate
endmodule
