// Logisim project Q3.circ as structural Verilog: 1 circuit, main circuit main
module main (
  input  A,
  input  B,
  input  C,
  output out_4
);

  wire and_1_out, and_2_out, and_3_out, not_1_out, not_2_out, or_1_out;

  not not_1 (not_1_out, C);
  not not_2 (not_2_out, B);
  buf and_1 (and_1_out, A);  // AND_Gate
  and and_2 (and_2_out, B, not_1_out);
  and and_3 (and_3_out, not_2_out, C);
  or or_1 (or_1_out, and_2_out, and_3_out);
  and and_4 (out_4, and_1_out, or_1_out);

  // Notes on the sheet:
  //   Question 3
endmodule
