// Logisim project Q4.circ as structural Verilog: 1 circuit, main circuit main
module main (
  input  A,
  input  B,
  input  C,
  output out_4
);

  wire not_1_out, not_2_out, or_1_out, or_2_out, or_3_out;

  not not_1 (not_1_out, A);
  not not_2 (not_2_out, B);
  or or_1 (or_1_out, A, B);
  or or_2 (or_2_out, A, C);
  or or_3 (or_3_out, not_1_out, not_2_out);
  and and_1 (out_4, or_1_out, or_2_out, or_3_out);

  // Notes on the sheet:
  //   Question 4
endmodule
