// Logisim project add.circ as structural Verilog: 1 circuit, main circuit main
module main (
  input  cin,
  input  a,
  input  b,
  output sum,
  output cout
);

  wire hadd_circ_1_carry, hadd_circ_1_sum, hadd_circ_2_carry;

  hadd_circ hadd_circ_1 (.a(a), .b(b), .sum(hadd_circ_1_sum), .carry(hadd_circ_1_carry));
  hadd_circ hadd_circ_2 (.a(cin), .b(hadd_circ_1_sum), .sum(sum), .carry(hadd_circ_2_carry));
  or or_1 (cout, hadd_circ_2_carry, hadd_circ_1_carry);
endmodule
