// Logisim project add8-1.circ as structural Verilog: 1 circuit, main circuit main
module main (
  input  [7:0] arg2,
  input  [7:0] arg1,
  output [7:0] suum,
  output cout
);

  wire main_1_carry;

  add4_main main_1 (.A(arg1[3:0]), .B(arg2[3:0]), .Sum(suum[3:0]), .Carry(main_1_carry));  // open: cin
  add4_main main_2 (.cin(main_1_carry), .A(arg1[7:4]), .B(arg2[7:4]), .Sum(suum[7:4]), .Carry(cout));
endmodule
