// Logisim project alu.circ as structural Verilog: 1 circuit, main circuit main
module main (
  input  [7:0] in_1,
  input  [7:0] in_2,
  input  [1:0] in_3,
  output [7:0] out_4
);

  wire [7:0] divider_1_out, multiplier_1_out, multiplier_2_out, subtractor_1_out;

  Subtractor subtractor_1 (.a(in_1), .b(in_2), .out(subtractor_1_out));  // open: bin, bout
  Multiplier multiplier_1 (.a(in_2), .b(in_1), .out(multiplier_1_out));  // open: cin, cout
  Multiplier multiplier_2 (.a(in_2), .b(in_1), .out(multiplier_2_out));  // open: cin, cout
  Divider divider_1 (.a(in_2), .b(in_1), .out(divider_1_out));  // open: upper, rem
  Multiplexer #(.select(2), .width(8)) multiplexer_1 (
    .in0(subtractor_1_out), .in1(multiplier_1_out), .in2(multiplier_2_out), .in3(divider_1_out), .out(out_4),
    .sel(in_3));  // open: en
endmodule
