// Logisim project hadd.circ as structural Verilog
module hadd_circ (
  input  a,
  input  b,
  output sum,
  output carry
);

  wire and_2_out, and_3_out, not_1_out, not_2_out;

  not not_1 (not_1_out, a);
  not not_2 (not_2_out, b);
  and and_1 (carry, a, b);
  and and_2 (and_2_out, not_1_out, b);
  and and_3 (and_3_out, a, not_2_out);
  or or_1 (sum, and_2_out, and_3_out);
endmodule
